# Fritzing sketch RGB-LED (saved by Fritzing 0.7.7b)
breadboards: 1

parts:
  Arduino1 = Arduino
  R1 = Rotary Potentiometer (Small) [maximum_resistance=100kΩ]
  R2 = Rotary Potentiometer (Small) [maximum_resistance=100kΩ]
  R3 = Rotary Potentiometer (Small) [maximum_resistance=100kΩ]
  R5 = Resistor [tolerance=±5% resistance=220 package=THT]
  R6 = Resistor [tolerance=±5% resistance=220 package=THT]
  R4 = Resistor [tolerance=±5% resistance=220 package=THT]
  LED1 = RGB LED - (4 legs) [package="5 mm [THT]"]

nets:
  N1: Arduino1.GND, R1.leg2, R2.leg2, R3.leg2
  N2: Arduino1.D11, R5.Pin_0
  N3: Arduino1.D10, R4.Pin_0
  N4: Arduino1.D9, R6.Pin_0
  N5: Arduino1.+5V, R1.leg1, R2.leg1, R3.leg1, LED1.common_anode
  N6: Arduino1.A1, R1.wiper
  N7: Arduino1.A3, R2.wiper
  N8: Arduino1.A5, R3.wiper
  N9: R5.Pin_1, LED1.green_cathode
  N10: R6.Pin_1, LED1.red_cathode
  N11: R4.Pin_1, LED1.blue_cathode
